// Logisim project CSE231L.1 Project Group 5 (1).circ as structural Verilog: 4 circuits, main circuit main
module main (
  input  I0,
  input  I1,
  input  I2,
  input  I3,
  input  I4,
  input  I5,
  input  I6,
  input  I7,
  input  I8,
  input  I9,
  input  in_11,
  output Y0,
  output Y1,
  output Y2,
  output Y3,
  output C,
  output [19:0] out_17,
  output [19:0] out_18
);

  wire A, B, C_t, D, demultiplexer_1_out0, demultiplexer_1_out1, or_6_out;

  or or_1 (C, I0, I1, I2, I3, I4, I5, I6, I7, I8, I9);
  D_Flip_Flop d_ff_1 (.clk(demultiplexer_1_out0), .D(A), .Q(out_18[16]));  // open: Qn, preset, en, reset
  D_Flip_Flop d_ff_2 (.clk(demultiplexer_1_out0), .D(B), .Q(out_18[17]));  // open: Qn, preset, en, reset
  D_Flip_Flop d_ff_3 (.clk(demultiplexer_1_out0), .D(C_t), .Q(out_18[18]));  // open: Qn, preset, en, reset
  D_Flip_Flop d_ff_4 (.clk(demultiplexer_1_out0), .D(D), .Q(out_18[19]));  // open: Qn, preset, en, reset
  D_Flip_Flop d_ff_5 (.clk(demultiplexer_1_out0), .D(out_18[16]), .Q(out_18[12]));  // open: Qn, preset, en, reset
  D_Flip_Flop d_ff_6 (.clk(demultiplexer_1_out0), .D(out_18[17]), .Q(out_18[13]));  // open: Qn, preset, en, reset
  D_Flip_Flop d_ff_7 (.clk(demultiplexer_1_out0), .D(out_18[18]), .Q(out_18[14]));  // open: Qn, preset, en, reset
  D_Flip_Flop d_ff_8 (.clk(demultiplexer_1_out0), .D(out_18[19]), .Q(out_18[15]));  // open: Qn, preset, en, reset
  D_Flip_Flop d_ff_9 (.clk(demultiplexer_1_out0), .D(out_18[12]), .Q(out_18[8]));  // open: Qn, preset, en, reset
  D_Flip_Flop d_ff_10 (.clk(demultiplexer_1_out0), .D(out_18[13]), .Q(out_18[9]));  // open: Qn, preset, en, reset
  D_Flip_Flop d_ff_11 (.clk(demultiplexer_1_out0), .D(out_18[14]), .Q(out_18[10]));  // open: Qn, preset, en, reset
  D_Flip_Flop d_ff_12 (.clk(demultiplexer_1_out0), .D(out_18[15]), .Q(out_18[11]));  // open: Qn, preset, en, reset
  or or_2 (A, I1, I3, I5, I7, I9);
  D_Flip_Flop d_ff_13 (.clk(demultiplexer_1_out0), .D(out_18[8]), .Q(out_18[4]));  // open: Qn, preset, en, reset
  D_Flip_Flop d_ff_14 (.clk(demultiplexer_1_out0), .D(out_18[9]), .Q(out_18[5]));  // open: Qn, preset, en, reset
  D_Flip_Flop d_ff_15 (.clk(demultiplexer_1_out0), .D(out_18[10]), .Q(out_18[6]));  // open: Qn, preset, en, reset
  D_Flip_Flop d_ff_16 (.clk(demultiplexer_1_out0), .D(out_18[11]), .Q(out_18[7]));  // open: Qn, preset, en, reset
  or or_3 (B, I2, I3, I6, I7);
  or or_4 (C_t, I4, I5, I6, I7);
  or or_5 (D, I8, I9);
  D_Flip_Flop d_ff_17 (.clk(demultiplexer_1_out0), .D(out_18[4]), .Q(out_18[0]));  // open: Qn, preset, en, reset
  D_Flip_Flop d_ff_18 (.clk(demultiplexer_1_out0), .D(out_18[5]), .Q(out_18[1]));  // open: Qn, preset, en, reset
  D_Flip_Flop d_ff_19 (.clk(demultiplexer_1_out0), .D(out_18[6]), .Q(out_18[2]));  // open: Qn, preset, en, reset
  D_Flip_Flop d_ff_20 (.clk(demultiplexer_1_out0), .D(out_18[7]), .Q(out_18[3]));  // open: Qn, preset, en, reset
  or or_6 (or_6_out, D, C_t, B, A, I0);
  Demultiplexer demultiplexer_1 (
    .out0(demultiplexer_1_out0), .out1(demultiplexer_1_out1), .in(or_6_out), .sel(in_11), .en(1'b1));
  D_Flip_Flop d_ff_21 (.clk(or_6_out), .D(A), .Q(Y0));  // open: Qn, preset, en, reset
  D_Flip_Flop d_ff_22 (.clk(or_6_out), .D(B), .Q(Y1));  // open: Qn, preset, en, reset
  D_Flip_Flop d_ff_23 (.clk(or_6_out), .D(C_t), .Q(Y2));  // open: Qn, preset, en, reset
  D_Flip_Flop d_ff_24 (.clk(or_6_out), .D(D), .Q(Y3));  // open: Qn, preset, en, reset
  D_Flip_Flop d_ff_25 (.clk(demultiplexer_1_out1), .D(A), .Q(out_17[16]));  // open: Qn, preset, en, reset
  D_Flip_Flop d_ff_26 (.clk(demultiplexer_1_out1), .D(B), .Q(out_17[17]));  // open: Qn, preset, en, reset
  D_Flip_Flop d_ff_27 (.clk(demultiplexer_1_out1), .D(C_t), .Q(out_17[18]));  // open: Qn, preset, en, reset
  D_Flip_Flop d_ff_28 (.clk(demultiplexer_1_out1), .D(D), .Q(out_17[19]));  // open: Qn, preset, en, reset
  D_Flip_Flop d_ff_29 (.clk(demultiplexer_1_out1), .D(out_17[16]), .Q(out_17[12]));  // open: Qn, preset, en, reset
  D_Flip_Flop d_ff_30 (.clk(demultiplexer_1_out1), .D(out_17[17]), .Q(out_17[13]));  // open: Qn, preset, en, reset
  D_Flip_Flop d_ff_31 (.clk(demultiplexer_1_out1), .D(out_17[18]), .Q(out_17[14]));  // open: Qn, preset, en, reset
  D_Flip_Flop d_ff_32 (.clk(demultiplexer_1_out1), .D(out_17[19]), .Q(out_17[15]));  // open: Qn, preset, en, reset
  D_Flip_Flop d_ff_33 (.clk(demultiplexer_1_out1), .D(out_17[12]), .Q(out_17[8]));  // open: Qn, preset, en, reset
  D_Flip_Flop d_ff_34 (.clk(demultiplexer_1_out1), .D(out_17[13]), .Q(out_17[9]));  // open: Qn, preset, en, reset
  D_Flip_Flop d_ff_35 (.clk(demultiplexer_1_out1), .D(out_17[14]), .Q(out_17[10]));  // open: Qn, preset, en, reset
  D_Flip_Flop d_ff_36 (.clk(demultiplexer_1_out1), .D(out_17[15]), .Q(out_17[11]));  // open: Qn, preset, en, reset
  D_Flip_Flop d_ff_37 (.clk(demultiplexer_1_out1), .D(out_17[8]), .Q(out_17[4]));  // open: Qn, preset, en, reset
  D_Flip_Flop d_ff_38 (.clk(demultiplexer_1_out1), .D(out_17[9]), .Q(out_17[5]));  // open: Qn, preset, en, reset
  D_Flip_Flop d_ff_39 (.clk(demultiplexer_1_out1), .D(out_17[10]), .Q(out_17[6]));  // open: Qn, preset, en, reset
  D_Flip_Flop d_ff_40 (.clk(demultiplexer_1_out1), .D(out_17[11]), .Q(out_17[7]));  // open: Qn, preset, en, reset
  D_Flip_Flop d_ff_41 (.clk(demultiplexer_1_out1), .D(out_17[4]), .Q(out_17[0]));  // open: Qn, preset, en, reset
  D_Flip_Flop d_ff_42 (.clk(demultiplexer_1_out1), .D(out_17[5]), .Q(out_17[1]));  // open: Qn, preset, en, reset
  D_Flip_Flop d_ff_43 (.clk(demultiplexer_1_out1), .D(out_17[6]), .Q(out_17[2]));  // open: Qn, preset, en, reset
  D_Flip_Flop d_ff_44 (.clk(demultiplexer_1_out1), .D(out_17[7]), .Q(out_17[3]));  // open: Qn, preset, en, reset
endmodule

module _20_Bit_Comparator (
  input  [19:0] in_1,
  input  [19:0] in_2,
  input  in_3,
  output out_4
);

  wire comparator_1_eq;

  Comparator #(.width(20)) comparator_1 (.a(in_1), .b(in_2), .eq(comparator_1_eq));  // open: gt, lt
  D_Flip_Flop d_ff_1 (.clk(in_3), .D(comparator_1_eq), .Q(out_4));  // open: Qn, preset, en, reset
endmodule

module Seven_Segment_Display_Circuit (
  input  Y3,
  input  Y2,
  input  Y1,
  input  Y0,
  output A,
  output B,
  output C,
  output D,
  output E,
  output F,
  output G
);

  wire and_1_out, and_2_out, and_3_out, and_4_out, and_5_out, and_6_out, and_7_out, and_8_out, and_9_out,
       and_10_out, and_11_out, and_12_out, and_13_out, and_14_out, and_15_out, and_16_out, and_17_out,
       and_18_out, and_19_out, and_20_out, and_21_out, and_22_out, not_1_out, not_2_out, not_3_out, not_4_out;

  not not_1 (not_1_out, Y3);
  not not_2 (not_2_out, Y2);
  not not_3 (not_3_out, Y1);
  not not_4 (not_4_out, Y0);
  and and_1 (and_1_out, not_3_out, not_4_out);
  and and_2 (and_2_out, Y3, not_3_out);
  and and_3 (and_3_out, Y2, not_3_out);
  and and_4 (and_4_out, Y2, not_4_out);
  and and_5 (and_5_out, Y3, not_3_out);
  and and_6 (and_6_out, Y2, Y0);
  and and_7 (and_7_out, not_1_out, not_2_out, not_4_out);
  and and_8 (and_8_out, not_1_out, Y1);
  and and_9 (and_9_out, Y3, not_3_out);
  and and_10 (and_10_out, not_1_out, not_2_out);
  and and_11 (and_11_out, not_3_out, not_4_out);
  and and_12 (and_12_out, not_1_out, Y1, Y0);
  and and_13 (and_13_out, not_2_out, not_3_out, not_4_out);
  and and_14 (and_14_out, Y1, not_4_out);
  and and_15 (and_15_out, Y3, Y1);
  and and_16 (and_16_out, Y1, not_4_out);
  and and_17 (and_17_out, Y2, not_3_out, Y0);
  and and_18 (and_18_out, not_2_out, not_3_out, not_4_out);
  and and_19 (and_19_out, not_1_out, not_2_out, Y1);
  and and_20 (and_20_out, Y2, not_3_out);
  and and_21 (and_21_out, Y1, not_4_out);
  and and_22 (and_22_out, not_2_out, Y1);
  or or_1 (A, and_1_out, and_2_out, and_3_out, and_4_out);
  or or_2 (B, and_5_out, and_6_out, and_7_out, and_8_out);
  or or_3 (C, and_9_out, and_10_out, and_11_out, and_12_out);
  or or_4 (D, and_13_out, and_14_out, and_15_out);
  or or_5 (E, and_16_out, and_17_out, and_18_out, and_19_out);
  or or_6 (F, Y3, Y2, not_3_out, Y0);
  or or_7 (G, Y3, and_20_out, and_21_out, and_22_out);
endmodule

module Digital_Lock_Circuit (
  input  Mode
);

  wire _0_out, _1_out, _2_out, _3_out, _4_out, _5_out, _6_out, _7_out, _8_out, _9_out, Enter_out, main_1_c,
       main_1_y0, main_1_y1, main_1_y2, main_1_y3, n20_bit_comparator_1_out_4, not_1_out,
       seven_segment_display_circuit_1_a, seven_segment_display_circuit_1_b,
       seven_segment_display_circuit_1_c, seven_segment_display_circuit_1_d,
       seven_segment_display_circuit_1_e, seven_segment_display_circuit_1_f,
       seven_segment_display_circuit_1_g, seven_segment_display_circuit_2_a,
       seven_segment_display_circuit_2_b, seven_segment_display_circuit_2_c,
       seven_segment_display_circuit_2_d, seven_segment_display_circuit_2_e,
       seven_segment_display_circuit_2_f, seven_segment_display_circuit_2_g;
  wire [19:0] main_1_out_17, main_1_out_18;

  Button _0 (.out(_0_out));
  Button _1 (.out(_1_out));
  Button _2 (.out(_2_out));
  Button _3 (.out(_3_out));
  Button _4 (.out(_4_out));
  Button _5 (.out(_5_out));
  Button _6 (.out(_6_out));
  Button _7 (.out(_7_out));
  Button _8 (.out(_8_out));
  Button _9 (.out(_9_out));
  Button Enter (.out(Enter_out));
  main main_1 (
    .I0(_0_out), .I1(_1_out), .I2(_2_out), .I3(_3_out), .I4(_4_out), .I5(_5_out), .I6(_6_out), .I7(_7_out),
    .I8(_8_out), .I9(_9_out), .in_11(Mode), .out_17(main_1_out_17), .out_18(main_1_out_18), .Y0(main_1_y0),
    .Y1(main_1_y1), .Y2(main_1_y2), .Y3(main_1_y3), .C(main_1_c));
  Counter #(.width(4), .max('h5)) counter_1 (
    .D(4'b0101), .count(main_1_c), .clk(main_1_c), .clr(Enter_out));  // open: load, Q, carry
  _20_Bit_Comparator u_20_bit_comparator_1 (
    .in_1(main_1_out_18), .in_2(main_1_out_17), .out_4(n20_bit_comparator_1_out_4), .in_3(Enter_out));
  not not_1 (not_1_out, n20_bit_comparator_1_out_4);
  Seven_Segment_Display_Circuit seven_segment_display_circuit_1 (
    .A(seven_segment_display_circuit_1_a), .B(seven_segment_display_circuit_1_b),
    .C(seven_segment_display_circuit_1_c), .D(seven_segment_display_circuit_1_d),
    .E(seven_segment_display_circuit_1_e), .F(seven_segment_display_circuit_1_f),
    .G(seven_segment_display_circuit_1_g), .Y3(main_1_y3), .Y2(main_1_y2), .Y1(main_1_y1), .Y0(main_1_y0));
  Seven_Segment_Display_Circuit seven_segment_display_circuit_2 (
    .A(seven_segment_display_circuit_2_a), .B(seven_segment_display_circuit_2_b),
    .C(seven_segment_display_circuit_2_c), .D(seven_segment_display_circuit_2_d),
    .E(seven_segment_display_circuit_2_e), .F(seven_segment_display_circuit_2_f),
    .G(seven_segment_display_circuit_2_g), .Y3(1'b1), .Y2(1'b0), .Y1(1'b1), .Y0(not_1_out));
  _7_Segment_Display u_7_segment_display_1 (
    .g(seven_segment_display_circuit_1_g), .f(seven_segment_display_circuit_1_a),
    .a(seven_segment_display_circuit_1_b), .b(seven_segment_display_circuit_1_c),
    .e(seven_segment_display_circuit_1_d), .d(seven_segment_display_circuit_1_e),
    .c(seven_segment_display_circuit_1_f));  // open: dp
  _7_Segment_Display u_7_segment_display_2 (
    .g(seven_segment_display_circuit_2_g), .f(seven_segment_display_circuit_2_a),
    .a(seven_segment_display_circuit_2_b), .b(seven_segment_display_circuit_2_c),
    .e(seven_segment_display_circuit_2_d), .d(seven_segment_display_circuit_2_e),
    .c(seven_segment_display_circuit_2_f));  // open: dp

  // Notes on the sheet:
  //   Enter 0 for Mode 1 /Enter 1 for Mode 2
endmodule
